# Fritzing sketch Co-Pine-ON-and-Pine64 (saved by Fritzing 0.9.3b)
breadboards: 1

parts:
  IC_=_PIC_12F1501 = IC, DIP package, 8 pins [chip_label=MCU]
  R1 = Resistor [tolerance=±5% resistance=1k package=THT]
  R2 = Resistor [tolerance=±5% resistance=1k package=THT]
  R3 = Resistor [tolerance=±5% resistance=10 package=THT]
  LED1 = LED - 3mm [color="Yellow (595nm)" package="3 mm [THT]"]  # not connected

nets:
  N1: IC_=_PIC_12F1501.pin2, R2.Pin_1
  N2: IC_=_PIC_12F1501.pin3, R3.Pin_0
  N3: IC_=_PIC_12F1501.pin5, R1.Pin_0

notes:
  Yellow, 3mm LED
  IC = PIC 12F1501
  EXP
